// Logisim project 2^nmod5.circ as structural Verilog: 1 circuit, main circuit mod5
module mod5 (
  input  In,
  output S0,
  output S1,
  output S2,
  output S3,
  output S4
);

  wire _1_q, _2_q, _3_q, _4_q, and_1_out, and_2_out, and_3_out, and_6_out, clock_1_out, not_1_out, not_2_out,
       not_3_out, not_4_out, not_5_out, not_6_out, not_7_out, not_8_out, not_9_out, not_10_out, not_11_out,
       not_12_out, or_1_out, or_2_out;

  Clock clock_1 (.out(clock_1_out));
  Register #(.width(1)) _0 (.D(S0), .Q(S0), .clk(clock_1_out));  // open: en, clr
  Register #(.width(1)) _1 (.D(S1), .Q(_1_q), .clk(clock_1_out));  // open: en, clr
  Register #(.width(1)) _2 (.D(S2), .Q(_2_q), .clk(clock_1_out));  // open: en, clr
  Register #(.width(1)) _3 (.D(S3), .Q(_3_q), .clk(clock_1_out));  // open: en, clr
  Register #(.width(1)) _4 (.D(S4), .Q(_4_q), .clk(clock_1_out));  // open: en, clr
  not not_1 (not_1_out, S0);
  not not_2 (not_2_out, _1_q);
  not not_3 (not_3_out, _2_q);
  not not_4 (not_4_out, _3_q);
  not not_5 (not_5_out, _4_q);
  or or_1 (or_1_out, _1_q, _4_q);
  not not_6 (not_6_out, In);
  or or_2 (or_2_out, _2_q, _3_q);
  not not_7 (not_7_out, In);
  not not_8 (not_8_out, S0);
  not not_9 (not_9_out, _1_q);
  not not_10 (not_10_out, _2_q);
  not not_11 (not_11_out, _3_q);
  not not_12 (not_12_out, _4_q);
  and and_1 (and_1_out, In, not_1_out, not_2_out, not_3_out, not_4_out, not_5_out);
  and and_2 (and_2_out, or_1_out, not_6_out);
  and and_3 (and_3_out, or_1_out, In);
  and and_4 (S4, or_2_out, not_6_out);
  and and_5 (S3, or_2_out, In);
  and and_6 (and_6_out, not_7_out, not_8_out, not_9_out, not_10_out, not_11_out, not_12_out);
  or or_3 (S1, and_6_out, and_2_out);
  or or_4 (S2, and_1_out, and_3_out);
endmodule
