// Logisim project ALU.circ as structural Verilog: 1 circuit, main circuit alu
module alu (
  input  [3:0] A,
  input  [3:0] B,
  input  [1:0] ALUOp,
  output [3:0] out_4
);

  wire ADD, AND, not_1_out, not_2_out, not_3_out, not_4_out, OR, SUB;
  wire [3:0] adder_1_out, and_1_out, or_1_out, subtractor_1_out;

  Adder #(.width(4)) adder_1 (.a(A), .b(B), .out(adder_1_out));  // open: cin, cout
  Subtractor #(.width(4)) subtractor_1 (.a(A), .b(B), .out(subtractor_1_out));  // open: bin, bout
  and and_1 (and_1_out[0], A[0], B[0]);
  and and_2 (and_1_out[1], A[1], B[1]);
  and and_3 (and_1_out[2], A[2], B[2]);
  and and_4 (and_1_out[3], A[3], B[3]);
  or or_1 (or_1_out[0], A[0], B[0]);
  or or_2 (or_1_out[1], A[1], B[1]);
  or or_3 (or_1_out[2], A[2], B[2]);
  or or_4 (or_1_out[3], A[3], B[3]);
  not not_1 (not_1_out, ALUOp[0]);
  not not_2 (not_2_out, ALUOp[1]);
  assign out_4 = ADD ? adder_1_out : 4'bz;  // Controlled_Buffer controlled_buffer_1
  assign out_4 = SUB ? subtractor_1_out : 4'bz;  // Controlled_Buffer controlled_buffer_2
  assign out_4 = AND ? and_1_out : 4'bz;  // Controlled_Buffer controlled_buffer_3
  assign out_4 = OR ? or_1_out : 4'bz;  // Controlled_Buffer controlled_buffer_4
  and and_5 (OR, ALUOp[0], ALUOp[1]);
  and and_6 (ADD, not_1_out, not_2_out);
  not not_3 (not_3_out, ALUOp[0]);
  not not_4 (not_4_out, ALUOp[1]);
  and and_7 (AND, not_3_out, ALUOp[1]);
  and and_8 (SUB, ALUOp[0], not_4_out);

  // Other names for the same wires on the sheet: _0 = ALUOp[0]; _1 = ALUOp[1]
endmodule
