// Logisim project CPU.circ as structural Verilog: 8 circuits, main circuit IFU
module IFU (
  input  JR,
  input  RESET,
  input  [31:0] inpc,
  input  ZERO,
  input  j_PC,
  input  nPC_SeL,
  input  [15:0] IMM16,
  output [31:0] pc,
  output [31:0] out_9
);

  wire and_1_out, \begin , clock_1_out;
  wire [3:0] PC_28_31;
  wire [27:0] PC_q;
  wire [31:0] adder_2_out, bit_extender_1_out, multiplexer_1_out, multiplexer_2_out, multiplexer_3_out,
       multiplexer_4_out, shifter_1_out;

  Clock clock_1 (.out(clock_1_out));
  Register #(.width(32)) u_PC (
    .D(multiplexer_3_out), .Q({PC_28_31, PC_q}), .clk(clock_1_out), .clr(RESET));  // open: en
  assign bit_extender_1_out = {{16{IMM16[15]}}, IMM16};  // Bit_Extender bit_extender_1
  Comparator #(.width(32)) comparator_1 (.a({32{1'b0}}), .b({PC_28_31, PC_q}), .eq(\begin ));  // open: gt, lt
  Shifter #(.width(32)) shifter_1 (.in(bit_extender_1_out), .\dist (5'b00010), .out(shifter_1_out));
  Multiplexer #(.width(32)) multiplexer_1 (
    .in0(32'h4), .in1(32'h3004), .out(multiplexer_1_out), .sel(\begin ));  // open: en
  Adder #(.width(32)) adder_1 (.a(multiplexer_1_out), .b({PC_28_31, PC_q}), .out(pc));  // open: cin, cout
  Adder #(.width(32)) adder_2 (.a(pc), .b(shifter_1_out), .out(adder_2_out));  // open: cin, cout
  Multiplexer #(.width(32)) multiplexer_2 (
    .in0(pc), .in1(adder_2_out), .out(multiplexer_2_out), .sel(and_1_out));  // open: en
  and and_1 (and_1_out, ZERO, nPC_SeL);
  ROM #(.addrWidth(5), .dataWidth(32)) rom_1 (.addr(PC_q[6:2]), .data(out_9));  // open: sel
  Multiplexer #(.width(32)) multiplexer_3 (
    .in0(multiplexer_4_out), .in1(inpc), .out(multiplexer_3_out), .sel(JR));  // open: en
  Multiplexer #(.width(32)) multiplexer_4 (
    .in0(multiplexer_2_out), .in1({PC_28_31, out_9[25:0], 2'b00}), .out(multiplexer_4_out), .sel(j_PC));  // open: en

  // Notes on the sheet:
  //   IM
  //   contents of rom_1 (hex, n*v repeats v):
  //   c000c06 3c05f010 34a5f000 ac050000 84030000 84040002 3e00008
endmodule

module ALU (
  input  [1:0] ALUOp,
  input  [31:0] in_2,
  input  [31:0] in_3,
  output [31:0] out_4,
  output ZERO
);

  wire [31:0] adder_1_out, or_1_out, subtractor_1_out, xor_1_out;

  Adder #(.width(32)) adder_1 (.a(in_2), .b(in_3), .out(adder_1_out));  // open: cin, cout
  Subtractor #(.width(32)) subtractor_1 (.a(in_2), .b(in_3), .out(subtractor_1_out));  // open: bin, bout
  assign or_1_out = in_2 | in_3;  // OR_Gate or_1, 32 bits wide
  assign xor_1_out = in_2 ^ in_3;  // XOR_Gate xor_1, 32 bits wide
  Comparator #(.width(32), .mode("unsigned")) comparator_1 (.a(in_2), .b(in_3), .eq(ZERO));  // open: gt, lt
  Multiplexer #(.select(2), .width(32), .disabled(0)) multiplexer_1 (
    .in0(adder_1_out), .in1(subtractor_1_out), .in2(or_1_out), .in3(xor_1_out), .out(out_4), .sel(ALUOp));  // open: en

  // Other names for the same wires on the sheet: A[31:0] = in_2; B[31:0] = in_3; op[1:0] = ALUOp
endmodule

module GRF (
  input  [4:0] Rreg1,
  input  [4:0] Rreg2,
  input  [4:0] Wreg,
  input  RegWrite,
  input  in_5,
  input  [31:0] Wdata,
  output [31:0] Rdata1,
  output [31:0] Rdata2
);

  wire and_1_out, and_2_out, and_3_out, and_4_out, and_5_out, and_6_out, and_7_out, and_8_out, and_9_out,
       and_10_out, and_11_out, and_12_out, and_13_out, and_14_out, and_15_out, and_16_out, and_17_out,
       and_18_out, and_19_out, and_20_out, and_21_out, and_22_out, and_23_out, and_24_out, and_25_out,
       and_26_out, and_27_out, and_28_out, and_29_out, and_30_out, and_31_out, and_32_out, clock_1_out,
       decoder_1_out0, decoder_1_out1, decoder_1_out2, decoder_1_out3, decoder_1_out4, decoder_1_out5,
       decoder_1_out6, decoder_1_out7, decoder_1_out8, decoder_1_out9, decoder_1_out10, decoder_1_out11,
       decoder_1_out12, decoder_1_out13, decoder_1_out14, decoder_1_out15, decoder_1_out16, decoder_1_out17,
       decoder_1_out18, decoder_1_out19, decoder_1_out20, decoder_1_out21, decoder_1_out22, decoder_1_out23,
       decoder_1_out24, decoder_1_out25, decoder_1_out26, decoder_1_out27, decoder_1_out28, decoder_1_out29,
       decoder_1_out30, decoder_1_out31;
  wire [31:0] _0, _1, _2, _3, _4, _5, _6, _7, _8, _9, _10, _11, _12, _13, _14, _15, _16, _17, _18, _19, _20,
       _21, _22, _23, _24, _25, _26, _27, _28, _29, _30, _31;

  Clock clock_1 (.out(clock_1_out));
  Decoder #(.select(5)) decoder_1 (
    .out0(decoder_1_out0), .out1(decoder_1_out1), .out2(decoder_1_out2), .out3(decoder_1_out3),
    .out4(decoder_1_out4), .out5(decoder_1_out5), .out6(decoder_1_out6), .out7(decoder_1_out7),
    .out8(decoder_1_out8), .out9(decoder_1_out9), .out10(decoder_1_out10), .out11(decoder_1_out11),
    .out12(decoder_1_out12), .out13(decoder_1_out13), .out14(decoder_1_out14), .out15(decoder_1_out15),
    .out16(decoder_1_out16), .out17(decoder_1_out17), .out18(decoder_1_out18), .out19(decoder_1_out19),
    .out20(decoder_1_out20), .out21(decoder_1_out21), .out22(decoder_1_out22), .out23(decoder_1_out23),
    .out24(decoder_1_out24), .out25(decoder_1_out25), .out26(decoder_1_out26), .out27(decoder_1_out27),
    .out28(decoder_1_out28), .out29(decoder_1_out29), .out30(decoder_1_out30), .out31(decoder_1_out31),
    .sel(Wreg));  // open: en
  buf and_1 (and_1_out, decoder_1_out0);  // AND_Gate
  and and_2 (and_2_out, decoder_1_out1, RegWrite);
  and and_3 (and_3_out, decoder_1_out2, RegWrite);
  and and_4 (and_4_out, decoder_1_out3, RegWrite);
  and and_5 (and_5_out, decoder_1_out4, RegWrite);
  and and_6 (and_6_out, decoder_1_out5, RegWrite);
  and and_7 (and_7_out, decoder_1_out6, RegWrite);
  and and_8 (and_8_out, decoder_1_out7, RegWrite);
  and and_9 (and_9_out, decoder_1_out8, RegWrite);
  and and_10 (and_10_out, decoder_1_out9, RegWrite);
  and and_11 (and_11_out, decoder_1_out10, RegWrite);
  and and_12 (and_12_out, decoder_1_out11, RegWrite);
  and and_13 (and_13_out, decoder_1_out12, RegWrite);
  and and_14 (and_14_out, decoder_1_out13, RegWrite);
  and and_15 (and_15_out, decoder_1_out14, RegWrite);
  and and_16 (and_16_out, decoder_1_out15, RegWrite);
  and and_17 (and_17_out, decoder_1_out16, RegWrite);
  and and_18 (and_18_out, decoder_1_out17, RegWrite);
  and and_19 (and_19_out, decoder_1_out18, RegWrite);
  and and_20 (and_20_out, decoder_1_out19, RegWrite);
  and and_21 (and_21_out, decoder_1_out20, RegWrite);
  and and_22 (and_22_out, decoder_1_out21, RegWrite);
  and and_23 (and_23_out, decoder_1_out22, RegWrite);
  and and_24 (and_24_out, decoder_1_out23, RegWrite);
  and and_25 (and_25_out, decoder_1_out24, RegWrite);
  and and_26 (and_26_out, decoder_1_out25, RegWrite);
  and and_27 (and_27_out, decoder_1_out26, RegWrite);
  and and_28 (and_28_out, decoder_1_out27, RegWrite);
  and and_29 (and_29_out, decoder_1_out28, RegWrite);
  and and_30 (and_30_out, decoder_1_out29, RegWrite);
  and and_31 (and_31_out, decoder_1_out30, RegWrite);
  and and_32 (and_32_out, decoder_1_out31, RegWrite);
  Register #(.width(32)) u__0 (.D({32{1'b0}}), .en(and_1_out), .Q(_0), .clk(clock_1_out), .clr(in_5));
  Register #(.width(32)) u__1 (.D(Wdata), .en(and_2_out), .Q(_1), .clk(clock_1_out), .clr(in_5));
  Register #(.width(32)) u__2 (.D(Wdata), .en(and_3_out), .Q(_2), .clk(clock_1_out), .clr(in_5));
  Register #(.width(32)) u__3 (.D(Wdata), .en(and_4_out), .Q(_3), .clk(clock_1_out), .clr(in_5));
  Register #(.width(32)) u__4 (.D(Wdata), .en(and_5_out), .Q(_4), .clk(clock_1_out), .clr(in_5));
  Register #(.width(32)) u__5 (.D(Wdata), .en(and_6_out), .Q(_5), .clk(clock_1_out), .clr(in_5));
  Register #(.width(32)) u__6 (.D(Wdata), .en(and_7_out), .Q(_6), .clk(clock_1_out), .clr(in_5));
  Register #(.width(32)) u__7 (.D(Wdata), .en(and_8_out), .Q(_7), .clk(clock_1_out), .clr(in_5));
  Register #(.width(32)) u__8 (.D(Wdata), .en(and_9_out), .Q(_8), .clk(clock_1_out), .clr(in_5));
  Register #(.width(32)) u__9 (.D(Wdata), .en(and_10_out), .Q(_9), .clk(clock_1_out), .clr(in_5));
  Register #(.width(32)) u__10 (.D(Wdata), .en(and_11_out), .Q(_10), .clk(clock_1_out), .clr(in_5));
  Register #(.width(32)) u__11 (.D(Wdata), .en(and_12_out), .Q(_11), .clk(clock_1_out), .clr(in_5));
  Register #(.width(32)) u__12 (.D(Wdata), .en(and_13_out), .Q(_12), .clk(clock_1_out), .clr(in_5));
  Register #(.width(32)) u__13 (.D(Wdata), .en(and_14_out), .Q(_13), .clk(clock_1_out), .clr(in_5));
  Register #(.width(32)) u__14 (.D(Wdata), .en(and_15_out), .Q(_14), .clk(clock_1_out), .clr(in_5));
  Register #(.width(32)) u__15 (.D(Wdata), .en(and_16_out), .Q(_15), .clk(clock_1_out), .clr(in_5));
  Register #(.width(32)) u__16 (.D(Wdata), .en(and_17_out), .Q(_16), .clk(clock_1_out), .clr(in_5));
  Register #(.width(32)) u__17 (.D(Wdata), .en(and_18_out), .Q(_17), .clk(clock_1_out), .clr(in_5));
  Register #(.width(32)) u__18 (.D(Wdata), .en(and_19_out), .Q(_18), .clk(clock_1_out), .clr(in_5));
  Register #(.width(32)) u__19 (.D(Wdata), .en(and_20_out), .Q(_19), .clk(clock_1_out), .clr(in_5));
  Register #(.width(32)) u__20 (.D(Wdata), .en(and_21_out), .Q(_20), .clk(clock_1_out), .clr(in_5));
  Register #(.width(32)) u__21 (.D(Wdata), .en(and_22_out), .Q(_21), .clk(clock_1_out), .clr(in_5));
  Register #(.width(32)) u__22 (.D(Wdata), .en(and_23_out), .Q(_22), .clk(clock_1_out), .clr(in_5));
  Register #(.width(32)) u__23 (.D(Wdata), .en(and_24_out), .Q(_23), .clk(clock_1_out), .clr(in_5));
  Register #(.width(32)) u__24 (.D(Wdata), .en(and_25_out), .Q(_24), .clk(clock_1_out), .clr(in_5));
  Register #(.width(32)) u__25 (.D(Wdata), .en(and_26_out), .Q(_25), .clk(clock_1_out), .clr(in_5));
  Register #(.width(32)) u__26 (.D(Wdata), .en(and_27_out), .Q(_26), .clk(clock_1_out), .clr(in_5));
  Register #(.width(32)) u__27 (.D(Wdata), .en(and_28_out), .Q(_27), .clk(clock_1_out), .clr(in_5));
  Register #(.width(32)) u__28 (.D(Wdata), .en(and_29_out), .Q(_28), .clk(clock_1_out), .clr(in_5));
  Register #(.width(32)) u__29 (.D(Wdata), .en(and_30_out), .Q(_29), .clk(clock_1_out), .clr(in_5));
  Register #(.width(32)) u__30 (.D(Wdata), .en(and_31_out), .Q(_30), .clk(clock_1_out), .clr(in_5));
  Register #(.width(32)) u__31 (.D(Wdata), .en(and_32_out), .Q(_31), .clk(clock_1_out), .clr(in_5));
  Multiplexer #(.select(5), .width(32)) multiplexer_1 (
    .in0(_0), .in1(_1), .in2(_2), .in3(_3), .in4(_4), .in5(_5), .in6(_6), .in7(_7), .in8(_8), .in9(_9),
    .in10(_10), .in11(_11), .in12(_12), .in13(_13), .in14(_14), .in15(_15), .in16(_16), .in17(_17),
    .in18(_18), .in19(_19), .in20(_20), .in21(_21), .in22(_22), .in23(_23), .in24(_24), .in25(_25),
    .in26(_26), .in27(_27), .in28(_28), .in29(_29), .in30(_30), .in31(_31), .out(Rdata1), .sel(Rreg1));  // open: en
  Multiplexer #(.select(5), .width(32)) multiplexer_2 (
    .in0(_0), .in1(_1), .in2(_2), .in3(_3), .in4(_4), .in5(_5), .in6(_6), .in7(_7), .in8(_8), .in9(_9),
    .in10(_10), .in11(_11), .in12(_12), .in13(_13), .in14(_14), .in15(_15), .in16(_16), .in17(_17),
    .in18(_18), .in19(_19), .in20(_20), .in21(_21), .in22(_22), .in23(_23), .in24(_24), .in25(_25),
    .in26(_26), .in27(_27), .in28(_28), .in29(_29), .in30(_30), .in31(_31), .out(Rdata2), .sel(Rreg2));  // open: en

  // Other names for the same wires on the sheet: R1[4:0] = Rreg1; R2[4:0] = Rreg2
endmodule

module DM (
  input  [31:0] Address,
  input  [31:0] WriteData,
  input  halfword,
  input  MemWrite,
  input  in_5,
  output [31:0] ReadData,
  output [4:0] out_7
);

  wire clock_1_out;
  wire [15:0] ram_1_data, ram_1_data_2;
  wire [31:0] ext_1_out_3, ext_2_out_3, multiplexer_1_out;

  Clock clock_1 (.out(clock_1_out));
  RAM #(.addrWidth(5), .dataWidth(32), .bus("separate")) ram_1 (
    .addr(Address[6:2]), .din(WriteData), .data({ram_1_data_2, ram_1_data}), .str(MemWrite),
    .clk(clock_1_out), .clr(in_5));  // open: sel, ld
  EXT ext_1 (.IMM16(ram_1_data), .ExtOp(2'b01), .out_3(ext_1_out_3));
  EXT ext_2 (.IMM16(ram_1_data_2), .ExtOp(2'b01), .out_3(ext_2_out_3));
  Multiplexer #(.width(32)) multiplexer_1 (
    .in0(ext_1_out_3), .in1(ext_2_out_3), .out(multiplexer_1_out), .sel(Address[1]));  // open: en
  Multiplexer #(.width(32)) multiplexer_2 (
    .in0({ram_1_data_2, ram_1_data}), .in1(multiplexer_1_out), .out(ReadData), .sel(halfword));  // open: en

  assign out_7 = Address[6:2];

  // Other names for the same wires on the sheet: lh_high = Address[1]
endmodule

module Controller (
  input  [5:0] Opcode,
  input  [5:0] funct,
  output JR,
  output RegDst,
  output ALUSrc,
  output MemtoReg,
  output RegWrite,
  output MemWrite,
  output nPC_Sel,
  output [1:0] ExtOp,
  output [1:0] ALUOp,
  output j_PC,
  output halfword
);

  wire addu_out, and_2_out, and_3_out, jr_out, lw_out, not_1_out, not_2_out, not_3_out, not_4_out, not_5_out,
       not_6_out, not_7_out, not_8_out, not_9_out, not_10_out, not_11_out, not_12_out, ori_out, R, subu_out,
       xori_out;

  not not_1 (not_1_out, Opcode[4]);
  not not_2 (not_2_out, Opcode[5]);
  not not_3 (not_3_out, Opcode[3]);
  not not_4 (not_4_out, Opcode[1]);
  not not_5 (not_5_out, Opcode[2]);
  not not_6 (not_6_out, Opcode[0]);
  and ori (ori_out, Opcode[0], not_4_out, Opcode[2], Opcode[3], not_1_out, not_2_out);
  and lw (lw_out, Opcode[0], Opcode[1], not_5_out, not_3_out, not_1_out, Opcode[5]);
  and sw (MemWrite, Opcode[0], Opcode[1], not_5_out, Opcode[3], not_1_out, Opcode[5]);
  and beq (nPC_Sel, not_6_out, not_4_out, Opcode[2], not_3_out, not_1_out, not_2_out);
  and lui (ExtOp[1], Opcode[0], Opcode[1], Opcode[2], Opcode[3], not_1_out, not_2_out);
  and jal (j_PC, Opcode[0], Opcode[1], not_5_out, not_3_out, not_1_out, not_2_out);
  and xori (xori_out, not_2_out, not_1_out, Opcode[3], Opcode[2], Opcode[1], not_6_out);
  and lh (halfword, Opcode[0], not_4_out, not_5_out, not_3_out, not_1_out, Opcode[5]);
  and and_1 (R, not_6_out, not_4_out, not_5_out, not_3_out, not_1_out, not_2_out);
  not not_7 (not_7_out, funct[4]);
  not not_8 (not_8_out, funct[5]);
  not not_9 (not_9_out, funct[1]);
  not not_10 (not_10_out, funct[2]);
  not not_11 (not_11_out, funct[3]);
  not not_12 (not_12_out, funct[0]);
  and and_2 (and_2_out, addu_out, R);
  and addu (addu_out, funct[0], not_9_out, not_10_out, not_11_out, not_7_out, funct[5]);
  and subu (subu_out, funct[0], funct[1], not_10_out, not_11_out, not_7_out, funct[5]);
  and and_3 (and_3_out, subu_out, R);
  and u_jr (jr_out, not_12_out, not_9_out, not_10_out, funct[3], not_7_out, not_8_out);
  and and_4 (JR, jr_out, R);
  or or_1 (RegDst, and_2_out, and_3_out);
  or or_2 (ALUSrc, ori_out, lw_out, xori_out, MemWrite, ExtOp[1], halfword);
  or or_3 (MemtoReg, lw_out, halfword);
  or or_4 (RegWrite, and_2_out, and_3_out, ori_out, xori_out, lw_out, halfword, ExtOp[1], j_PC);
  or or_5 (ExtOp[0], lw_out, halfword, MemWrite);
  or or_6 (ALUOp[0], and_3_out, xori_out, nPC_Sel);
  or or_7 (ALUOp[1], ori_out, xori_out);

  // Other names for the same wires on the sheet: f0 = funct[0]; f1 = funct[1]; f2 = funct[2]; f3 = funct[3];
  //   f4 = funct[4]; f5 = funct[5]; op0 = Opcode[0]; op1 = Opcode[1]; op2 = Opcode[2]; op3 = Opcode[3];
  //   op4 = Opcode[4]; op5 = Opcode[5]
endmodule

module main (
  input  Reset,
  output [31:0] out_2,
  output out_3,
  output [4:0] out_4,
  output [31:0] out_5,
  output out_6,
  output [4:0] out_7,
  output [31:0] out_8
);

  wire ALUSrc, halfword, j_PC, JR, MemtoReg, nPC_Sel, RegDst, Zero;
  wire [1:0] ALUOp, ExtOp;
  wire [4:0] multiplexer_1_out, rd, rs, rt;
  wire [5:0] Func, op;
  wire [15:0] Imm16;
  wire [31:0] alu_1_out_4, dm_1_readdata, ext_1_out_3, grf_1_rdata1, multiplexer_3_out, multiplexer_4_out, PC;

  Multiplexer #(.width(5)) multiplexer_1 (.in0(rt), .in1(rd), .out(multiplexer_1_out), .sel(RegDst));  // open: en
  Multiplexer #(.width(5)) multiplexer_2 (
    .in0(multiplexer_1_out), .in1({5{1'b1}}), .out(out_4), .sel(j_PC));  // open: en
  IFU ifu_1 (
    .RESET(Reset), .ZERO(Zero), .nPC_SeL(nPC_Sel), .IMM16(Imm16), .out_9(out_2), .pc(PC), .j_PC(j_PC),
    .JR(JR), .inpc(grf_1_rdata1));
  GRF grf_1 (
    .Wreg(out_4), .RegWrite(out_3), .Rreg1(rs), .Wdata(out_5), .Rreg2(rt), .Rdata1(grf_1_rdata1),
    .Rdata2(out_8), .in_5(Reset));
  EXT ext_1 (.IMM16(Imm16), .ExtOp(ExtOp), .out_3(ext_1_out_3));
  Controller controller_1 (
    .Opcode(op), .funct(Func), .RegDst(RegDst), .ALUSrc(ALUSrc), .MemtoReg(MemtoReg), .RegWrite(out_3),
    .MemWrite(out_6), .nPC_Sel(nPC_Sel), .ExtOp(ExtOp), .ALUOp(ALUOp), .j_PC(j_PC), .halfword(halfword),
    .JR(JR));
  Multiplexer #(.width(32)) multiplexer_3 (
    .in0(out_8), .in1(ext_1_out_3), .out(multiplexer_3_out), .sel(ALUSrc));  // open: en
  IMsplitter imsplitter_1 (.in_1(out_2), .out_2(Imm16), .Func(Func), .rd(rd), .rt(rt), .rs(rs), .op(op));
  ALU alu_1 (.ALUOp(ALUOp), .in_2(grf_1_rdata1), .in_3(multiplexer_3_out), .out_4(alu_1_out_4), .ZERO(Zero));
  DM dm_1 (
    .Address(alu_1_out_4), .WriteData(out_8), .MemWrite(out_6), .ReadData(dm_1_readdata), .out_7(out_7),
    .in_5(Reset), .halfword(halfword));
  Multiplexer #(.width(32)) multiplexer_4 (
    .in0(alu_1_out_4), .in1(dm_1_readdata), .out(multiplexer_4_out), .sel(MemtoReg));  // open: en
  Multiplexer #(.width(32)) multiplexer_5 (.in0(multiplexer_4_out), .in1(PC), .out(out_5), .sel(j_PC));  // open: en

  // Other names for the same wires on the sheet: Instr[31:0] = out_2; MemAddr[4:0] = out_7; MemData[31:0] = out_8;
  //   MemWrite = out_6; RegAddr[4:0] = out_4; RegData[31:0] = out_5; RegWrite = out_3
endmodule

module EXT (
  input  [15:0] IMM16,
  input  [1:0] ExtOp,
  output [31:0] out_3
);

  wire [31:0] bit_extender_1_out, bit_extender_2_out, shifter_1_out;

  assign bit_extender_1_out = {{16{1'b0}}, IMM16};  // Bit_Extender bit_extender_1
  assign bit_extender_2_out = {{16{IMM16[15]}}, IMM16};  // Bit_Extender bit_extender_2
  Shifter #(.width(32)) shifter_1 (.in(bit_extender_2_out), .\dist (5'b10000), .out(shifter_1_out));
  Multiplexer #(.select(2), .width(32)) multiplexer_1 (
    .in0(bit_extender_1_out), .in1(bit_extender_2_out), .in2(shifter_1_out), .in3({32{1'b0}}), .out(out_3),
    .sel(ExtOp));  // open: en
endmodule

module IMsplitter (
  input  [31:0] in_1,
  output [15:0] out_2,
  output [5:0] Func,
  output [4:0] rd,
  output [4:0] rt,
  output [4:0] rs,
  output [5:0] op
);


  assign Func = in_1[5:0];
  assign op = in_1[31:26];
  assign out_2 = in_1[15:0];
  assign rd = in_1[15:11];
  assign rs = in_1[25:21];
  assign rt = in_1[20:16];
endmodule
