// Logisim project CRC.circ as structural Verilog: 2 circuits, main circuit 4bit
module _4bit (
  input  [3:0] A,
  input  [3:0] B,
  output [2:0] C,
  output out_4
);

  wire not_1_out;
  wire [2:0] xor_1_out;

  xor xor_1 (xor_1_out[0], A[0], B[0]);
  xor xor_2 (xor_1_out[1], A[1], B[1]);
  xor xor_3 (xor_1_out[2], A[2], B[2]);
  not not_1 (not_1_out, A[3]);
  assign C = A[3] ? xor_1_out : 3'bz;  // Controlled_Buffer controlled_buffer_1
  assign C = not_1_out ? A[2:0] : 3'bz;  // Controlled_Buffer controlled_buffer_2

  assign out_4 = A[3];

  // Other names for the same wires on the sheet: D = A[3]
endmodule

module CRC (
  input  [7:0] A,
  input  [3:0] B,
  output [10:0] out_3
);

  wire [2:0] n4bit_1_c, n4bit_2_c, n4bit_3_c, n4bit_4_c, n4bit_6_c, n4bit_7_c;
  wire [3:1] nN;

  _4bit u_4bit_1 (.A({nN, 1'b0}), .B(B), .C(n4bit_1_c));  // open: out_4
  _4bit u_4bit_2 (.A(A[7:4]), .B(B), .C(n4bit_2_c));  // open: out_4
  _4bit u_4bit_3 (.A({n4bit_1_c, 1'b0}), .B(B), .C(n4bit_3_c));  // open: out_4
  _4bit u_4bit_4 (.A({n4bit_2_c, A[3]}), .B(B), .C(n4bit_4_c));  // open: out_4
  _4bit u_4bit_5 (.A({n4bit_3_c, 1'b0}), .B(B), .C(out_3[2:0]));  // open: out_4
  _4bit u_4bit_6 (.A({n4bit_4_c, A[2]}), .B(B), .C(n4bit_6_c));  // open: out_4
  _4bit u_4bit_7 (.A({n4bit_6_c, A[1]}), .B(B), .C(n4bit_7_c));  // open: out_4
  _4bit u_4bit_8 (.A({n4bit_7_c, A[0]}), .B(B), .C(nN));  // open: out_4

  assign out_3[10:3] = A;

  // Other names for the same wires on the sheet: B4 = A[0]; Y[2:0] = out_3[2:0]; B3 = A[1]; B2 = A[2]; B1 = A[3]
endmodule
