// Logisim project SWAP.circ as structural Verilog: 5 circuits, main circuit 1bit_swap
module _1bit_swap (
  input  I1,
  input  I2,
  input  S,
  output O1,
  output O2
);

  wire not_1_out, not_2_out, T, xor_1_out;

  xor xor_1 (xor_1_out, I1, I2);
  assign O1 = not_1_out ? I1 : 1'bz;  // Controlled_Buffer controlled_buffer_1
  not not_1 (not_1_out, T);
  and and_1 (T, xor_1_out, S);
  assign O1 = T ? I2 : 1'bz;  // Controlled_Buffer controlled_buffer_2
  assign O2 = T ? I1 : 1'bz;  // Controlled_Buffer controlled_buffer_3
  assign O2 = not_2_out ? I2 : 1'bz;  // Controlled_Buffer controlled_buffer_4
  not not_2 (not_2_out, T);
endmodule

module appearance_1 (
  input  I1,
  input  I2,
  input  S,
  output O1,
  output O2
);

  _1bit_swap u_1bit_swap_1 (.I1(I1), .I2(I2), .S(S), .O1(O1), .O2(O2));
endmodule

module _4bit_swap (
  input  [3:0] A,
  input  [3:0] B,
  input  in_3,
  output [3:0] O1,
  output [3:0] O2
);

  _1bit_swap u_1bit_swap_1 (.I1(A[0]), .I2(B[0]), .S(in_3), .O1(O1[0]), .O2(O2[0]));
  _1bit_swap u_1bit_swap_2 (.I1(A[1]), .I2(B[1]), .S(in_3), .O1(O1[1]), .O2(O2[1]));
  _1bit_swap u_1bit_swap_3 (.I1(A[2]), .I2(B[2]), .S(in_3), .O1(O1[2]), .O2(O2[2]));
  _1bit_swap u_1bit_swap_4 (.I1(A[3]), .I2(B[3]), .S(in_3), .O1(O1[3]), .O2(O2[3]));
endmodule

module _4bit_sort (
  input  [3:0] A,
  input  [3:0] B,
  input  [3:0] C,
  input  [3:0] D,
  output [3:0] _1,
  output [3:0] _2,
  output [3:0] _3,
  output [3:0] _4
);

  wire comparator_1_gt, comparator_2_gt, comparator_3_gt, comparator_4_gt, comparator_5_gt, comparator_6_gt;
  wire [3:0] n4bit_swap_1_o1, n4bit_swap_1_o2, n4bit_swap_2_o1, n4bit_swap_2_o2, n4bit_swap_3_o1,
       n4bit_swap_3_o2, n4bit_swap_4_o2, n4bit_swap_5_o2;

  Comparator #(.width(4), .mode("unsigned")) comparator_1 (.a(A), .b(B), .gt(comparator_1_gt));  // open: eq, lt
  _4bit_swap u_4bit_swap_1 (.A(A), .B(B), .in_3(comparator_1_gt), .O1(n4bit_swap_1_o1), .O2(n4bit_swap_1_o2));
  Comparator #(.width(4), .mode("unsigned")) comparator_2 (
    .a(n4bit_swap_1_o1), .b(C), .gt(comparator_2_gt));  // open: eq, lt
  _4bit_swap u_4bit_swap_2 (
    .A(n4bit_swap_1_o1), .B(C), .in_3(comparator_2_gt), .O1(n4bit_swap_2_o1), .O2(n4bit_swap_2_o2));
  Comparator #(.width(4), .mode("unsigned")) comparator_3 (
    .a(n4bit_swap_2_o2), .b(n4bit_swap_1_o2), .gt(comparator_3_gt));  // open: eq, lt
  _4bit_swap u_4bit_swap_3 (
    .A(n4bit_swap_2_o2), .B(n4bit_swap_1_o2), .in_3(comparator_3_gt), .O1(n4bit_swap_3_o1),
    .O2(n4bit_swap_3_o2));
  Comparator #(.width(4), .mode("unsigned")) comparator_4 (
    .a(n4bit_swap_2_o1), .b(D), .gt(comparator_4_gt));  // open: eq, lt
  _4bit_swap u_4bit_swap_4 (.A(n4bit_swap_2_o1), .B(D), .in_3(comparator_4_gt), .O1(_1), .O2(n4bit_swap_4_o2));
  Comparator #(.width(4), .mode("unsigned")) comparator_5 (
    .a(n4bit_swap_4_o2), .b(n4bit_swap_3_o1), .gt(comparator_5_gt));  // open: eq, lt
  _4bit_swap u_4bit_swap_5 (
    .A(n4bit_swap_4_o2), .B(n4bit_swap_3_o1), .in_3(comparator_5_gt), .O1(_2), .O2(n4bit_swap_5_o2));
  _4bit_swap u_4bit_swap_6 (.A(n4bit_swap_5_o2), .B(n4bit_swap_3_o2), .in_3(comparator_6_gt), .O1(_3), .O2(_4));
  Comparator #(.width(4), .mode("unsigned")) comparator_6 (
    .a(n4bit_swap_5_o2), .b(n4bit_swap_3_o2), .gt(comparator_6_gt));  // open: eq, lt
endmodule

module appearance_2 (
  input  [3:0] A,
  input  [3:0] B,
  input  [3:0] C,
  input  [3:0] D,
  output [3:0] _1,
  output [3:0] _2,
  output [3:0] _3,
  output [3:0] _4
);

  _4bit_sort u_4bit_sort_1 (.A(A), .B(B), .C(C), .D(D), ._1(_1), ._2(_2), ._3(_3), ._4(_4));
endmodule
