// Logisim project fib challenge.circ as structural Verilog: 1 circuit, main circuit main
module main (
  input  [31:0] in_1,
  output [31:0] out_2
);

  wire clock_1_out, cnt, controlled_buffer_1_out, controlled_buffer_3_out, ctrl, even, not_1_out, not_2_out,
       not_3_out, not_4_out, not_5_out, not_6_out, not_7_out, not_8_out, or_1_out, start;
  wire [31:0] A00, A01, A10, A11, adder_1_out, controlled_buffer_2_out, controlled_buffer_5_out,
       controlled_buffer_7_out, controlled_buffer_9_out, controlled_buffer_11_out, controlled_buffer_13_out,
       counter_1_q, divider_1_out, IA00, IA01, IA10, IA11, Ires00, Ires01, Ires10, Ires11, multiplier_1_out,
       multiplier_2_out, multiplier_3_out, multiplier_4_out, multiplier_5_out, multiplier_6_out,
       multiplier_7_out, multiplier_8_out, multiplier_9_out, multiplier_10_out, multiplier_11_out,
       multiplier_12_out, multiplier_13_out, multiplier_14_out, multiplier_15_out, multiplier_16_out, n_q,
       res00, res01, res10, res11;
  wire [31:1] and_1_out;

  Clock clock_1 (.out(clock_1_out));
  Counter #(.width(32), .max('hffffffff)) counter_1 (
    .Q(counter_1_q), .clk(clock_1_out));  // open: load, D, count, carry, clr
  assign controlled_buffer_1_out = ctrl ? clock_1_out : 1'bz;  // Controlled_Buffer controlled_buffer_1
  Adder #(.width(32)) adder_1 (.a(in_1), .b(32'h1), .out(adder_1_out));  // open: cin, cout
  assign controlled_buffer_2_out = start ? adder_1_out : 32'bz;  // Controlled_Buffer controlled_buffer_2
  Comparator #(.width(32), .mode("unsigned")) comparator_1 (.a(counter_1_q), .b({32{1'b0}}), .eq(cnt));  // open: gt, lt
  not not_1 (not_1_out, start);
  not not_2 (not_2_out, start);
  assign controlled_buffer_3_out = or_1_out ? controlled_buffer_1_out : 1'bz;  // Controlled_Buffer controlled_buffer_3
  assign controlled_buffer_2_out = not_4_out ? divider_1_out : 32'bz;  // Controlled_Buffer controlled_buffer_4
  Register #(.width(32)) n (.D(controlled_buffer_2_out), .Q(n_q), .clk(controlled_buffer_1_out));  // open: en, clr
  assign controlled_buffer_5_out = start ? 32'h1 : 32'bz;  // Controlled_Buffer controlled_buffer_5
  assign controlled_buffer_5_out = not_1_out ? IA00 : 32'bz;  // Controlled_Buffer controlled_buffer_6
  Register #(.width(32)) A0_0 (.D(controlled_buffer_5_out), .Q(A00), .clk(controlled_buffer_1_out));  // open: en, clr
  assign controlled_buffer_7_out = start ? 32'h1 : 32'bz;  // Controlled_Buffer controlled_buffer_7
  Register #(.width(32)) A1_0 (.D(controlled_buffer_7_out), .Q(A10), .clk(controlled_buffer_1_out));  // open: en, clr
  assign controlled_buffer_7_out = not_2_out ? IA10 : 32'bz;  // Controlled_Buffer controlled_buffer_8
  or or_1 (or_1_out, even, start);
  assign controlled_buffer_9_out = start ? 32'h1 : 32'bz;  // Controlled_Buffer controlled_buffer_9
  not not_3 (not_3_out, start);
  Register #(.width(32)) res0_0 (
    .D(controlled_buffer_9_out), .Q(res00), .clk(controlled_buffer_3_out));  // open: en, clr
  assign controlled_buffer_9_out = not_3_out ? Ires00 : 32'bz;  // Controlled_Buffer controlled_buffer_10
  Register #(.width(32)) res1_0 (.D(Ires10), .Q(res10), .clk(controlled_buffer_3_out));  // open: en, clr
  not not_4 (not_4_out, start);
  Comparator #(.width(32), .mode("unsigned")) comparator_2 (.a(n_q), .b({32{1'b0}}), .eq(start));  // open: gt, lt
  assign controlled_buffer_11_out = start ? 32'h1 : 32'bz;  // Controlled_Buffer controlled_buffer_11
  not not_5 (not_5_out, start);
  assign controlled_buffer_11_out = not_5_out ? IA01 : 32'bz;  // Controlled_Buffer controlled_buffer_12
  assign controlled_buffer_13_out = start ? 32'h1 : 32'bz;  // Controlled_Buffer controlled_buffer_13
  not not_6 (not_6_out, start);
  assign controlled_buffer_13_out = not_6_out ? Ires11 : 32'bz;  // Controlled_Buffer controlled_buffer_14
  Divider #(.width(32)) divider_1 (.a(n_q), .b(32'h2), .out(divider_1_out));  // open: upper, rem
  Register #(.width(32)) A0_1 (.D(controlled_buffer_11_out), .Q(A01), .clk(controlled_buffer_1_out));  // open: en, clr
  Register #(.width(32)) A1_1 (.D(IA11), .Q(A11), .clk(controlled_buffer_1_out));  // open: en, clr
  Register #(.width(32)) res0_1 (.D(Ires01), .Q(res01), .clk(controlled_buffer_3_out));  // open: en, clr
  Register #(.width(32)) res1_1 (
    .D(controlled_buffer_13_out), .Q(res11), .clk(controlled_buffer_3_out));  // open: en, clr
  not not_7 (not_7_out, start);
  assign {and_1_out, even} = n_q & 32'h1;  // AND_Gate and_1, 32 bits wide
  or or_2 (ctrl, cnt, not_7_out);
  Multiplier #(.width(32)) multiplier_1 (.a(A00), .b(A00), .out(multiplier_1_out));  // open: cin, cout
  Multiplier #(.width(32)) multiplier_2 (.a(A01), .b(A10), .out(multiplier_2_out));  // open: cin, cout
  Multiplier #(.width(32)) multiplier_3 (.a(A10), .b(A00), .out(multiplier_3_out));  // open: cin, cout
  Multiplier #(.width(32)) multiplier_4 (.a(A11), .b(A10), .out(multiplier_4_out));  // open: cin, cout
  Multiplier #(.width(32)) multiplier_5 (.a(A00), .b(res00), .out(multiplier_5_out));  // open: cin, cout
  Multiplier #(.width(32)) multiplier_6 (.a(A01), .b(res10), .out(multiplier_6_out));  // open: cin, cout
  Multiplier #(.width(32)) multiplier_7 (.a(A10), .b(res00), .out(multiplier_7_out));  // open: cin, cout
  Multiplier #(.width(32)) multiplier_8 (.a(A11), .b(res10), .out(multiplier_8_out));  // open: cin, cout
  assign out_2 = start ? res11 : 32'bz;  // Controlled_Buffer controlled_buffer_15
  Adder #(.width(32)) adder_2 (.a(multiplier_1_out), .b(multiplier_2_out), .out(IA00));  // open: cin, cout
  Adder #(.width(32)) adder_3 (.a(multiplier_3_out), .b(multiplier_4_out), .out(IA10));  // open: cin, cout
  Adder #(.width(32)) adder_4 (.a(multiplier_5_out), .b(multiplier_6_out), .out(Ires00));  // open: cin, cout
  Adder #(.width(32)) adder_5 (.a(multiplier_7_out), .b(multiplier_8_out), .out(Ires10));  // open: cin, cout
  assign out_2 = not_8_out ? {32{1'b0}} : 32'bz;  // Controlled_Buffer controlled_buffer_16
  not not_8 (not_8_out, start);
  Multiplier #(.width(32)) multiplier_9 (.a(A00), .b(A01), .out(multiplier_9_out));  // open: cin, cout
  Multiplier #(.width(32)) multiplier_10 (.a(A01), .b(A11), .out(multiplier_10_out));  // open: cin, cout
  Multiplier #(.width(32)) multiplier_11 (.a(A10), .b(A01), .out(multiplier_11_out));  // open: cin, cout
  Multiplier #(.width(32)) multiplier_12 (.a(A11), .b(A11), .out(multiplier_12_out));  // open: cin, cout
  Multiplier #(.width(32)) multiplier_13 (.a(A00), .b(res01), .out(multiplier_13_out));  // open: cin, cout
  Multiplier #(.width(32)) multiplier_14 (.a(A01), .b(res11), .out(multiplier_14_out));  // open: cin, cout
  Multiplier #(.width(32)) multiplier_15 (.a(A10), .b(res01), .out(multiplier_15_out));  // open: cin, cout
  Multiplier #(.width(32)) multiplier_16 (.a(A11), .b(res11), .out(multiplier_16_out));  // open: cin, cout
  Adder #(.width(32)) adder_6 (.a(multiplier_9_out), .b(multiplier_10_out), .out(IA01));  // open: cin, cout
  Adder #(.width(32)) adder_7 (.a(multiplier_11_out), .b(multiplier_12_out), .out(IA11));  // open: cin, cout
  Adder #(.width(32)) adder_8 (.a(multiplier_13_out), .b(multiplier_14_out), .out(Ires01));  // open: cin, cout
  Adder #(.width(32)) adder_9 (.a(multiplier_15_out), .b(multiplier_16_out), .out(Ires11));  // open: cin, cout
endmodule
