// Logisim project fib.circ as structural Verilog: 1 circuit, main circuit main
module main (
  input  [2:0] In,
  output [3:0] Out
);

  wire clock_1_out, comparator_1_eq, comparator_2_eq, controlled_buffer_1_out, controlled_buffer_2_out,
       not_1_out, not_2_out, not_3_out, not_4_out;
  wire [2:0] counter_1_q;
  wire [3:0] adder_1_out, controlled_buffer_3_out, T1_q, T2_q;

  not not_1 (not_1_out, comparator_1_eq);
  assign controlled_buffer_1_out = not_1_out ? controlled_buffer_2_out : 1'bz;  // Controlled_Buffer controlled_buffer_1
  Clock clock_1 (.out(clock_1_out));
  not not_2 (not_2_out, comparator_2_eq);
  assign controlled_buffer_2_out = not_2_out ? clock_1_out : 1'bz;  // Controlled_Buffer controlled_buffer_2
  assign controlled_buffer_3_out = comparator_1_eq ? 4'b0001 : 4'bz;  // Controlled_Buffer controlled_buffer_3
  Counter #(.width(3), .max('h7)) counter_1 (
    .Q(counter_1_q), .clk(controlled_buffer_1_out));  // open: load, D, count, carry, clr
  Register #(.width(4)) T1 (.D(T2_q), .Q(T1_q), .clk(controlled_buffer_2_out));  // open: en, clr
  Register #(.width(4)) T2 (.D(controlled_buffer_3_out), .Q(T2_q), .clk(controlled_buffer_2_out));  // open: en, clr
  Comparator #(.width(4)) comparator_1 (.a(4'b0000), .b(T2_q), .eq(comparator_1_eq));  // open: gt, lt
  assign Out = comparator_2_eq ? T1_q : 4'bz;  // Controlled_Buffer controlled_buffer_4
  Comparator #(.width(3)) comparator_2 (.a(counter_1_q), .b(In), .eq(comparator_2_eq));  // open: gt, lt
  assign Out = not_3_out ? 4'b0000 : 4'bz;  // Controlled_Buffer controlled_buffer_5
  not not_3 (not_3_out, comparator_2_eq);
  not not_4 (not_4_out, comparator_1_eq);
  Adder #(.width(4)) adder_1 (.a(T1_q), .b(T2_q), .out(adder_1_out));  // open: cin, cout
  assign controlled_buffer_3_out = not_4_out ? adder_1_out : 4'bz;  // Controlled_Buffer controlled_buffer_6
endmodule
