// Logisim project fsm.circ as structural Verilog: 2 circuits, main circuit fsm
module fsm (
  input  CLR,
  input  [1:0] In,
  output out_3
);

  wire and_1_out, clock_1_out, register_1_q;
  wire [1:0] register_2_q, trans_1_out_3;

  Clock clock_1 (.out(clock_1_out));
  trans trans_1 (.state(register_2_q), .in(In), .out_3(trans_1_out_3));
  Register #(.width(1)) register_1 (.D(CLR), .Q(register_1_q), .clk(clock_1_out));  // open: en, clr
  Register #(.width(2)) register_2 (
    .D(trans_1_out_3), .Q(register_2_q), .clk(clock_1_out), .clr(and_1_out));  // open: en
  and and_1 (and_1_out, register_1_q, CLR);
  Comparator #(.width(2)) comparator_1 (.a(trans_1_out_3), .b(2'b11), .eq(out_3));  // open: gt, lt
endmodule

module trans (
  input  [1:0] state,
  input  [1:0] in,
  output [1:0] out_3
);

  wire and_1_out, and_2_out, and_3_out, and_4_out, not_1_out, not_2_out, not_3_out, not_4_out, not_5_out,
       not_6_out, not_7_out;

  not not_1 (not_1_out, state[1]);
  not not_2 (not_2_out, in[0]);
  not not_3 (not_3_out, state[0]);
  not not_4 (not_4_out, in[0]);
  not not_5 (not_5_out, in[1]);
  not not_6 (not_6_out, state[0]);
  not not_7 (not_7_out, in[0]);
  and and_1 (and_1_out, not_1_out, state[0], not_2_out);
  and and_2 (and_2_out, state[1], not_3_out, not_4_out);
  and and_3 (and_3_out, not_5_out, in[0]);
  and and_4 (and_4_out, state[1], not_6_out, not_7_out);
  or or_1 (out_3[1], and_1_out, and_2_out);
  or or_2 (out_3[0], and_3_out, and_4_out);
endmodule
